// Digital circuit UTS1_10.dig as structural Verilog
module UTS1_10 (
  input  w,
  input  x,
  input  y,
  input  z
);

  wire and_1_out, and_2_out, and_3_out, and_4_out, and_5_out, not_1_out, not_2_out, not_3_out, not_4_out,
       or_1_out;

  not not_1 (not_1_out, x);
  not not_2 (not_2_out, w);
  not not_3 (not_3_out, z);
  not not_4 (not_4_out, x);
  and and_1 (and_1_out, w, x, y, z);
  and and_2 (and_2_out, w, not_4_out);
  and and_3 (and_3_out, w, not_1_out, y);
  and and_4 (and_4_out, w, x, y);
  and and_5 (and_5_out, not_2_out, y, not_3_out);
  or or_1 (or_1_out, and_1_out, and_2_out, and_3_out, and_4_out, and_5_out);
  LED A (.in(or_1_out));

  // Notes on the sheet:
  //   NO 10.  wxyz + wx' + wx'y + wxy + w'yz'
  //   FATIMAH CAHYANI IRAWAN
endmodule
