// Digital circuit UTS1_11.dig as structural Verilog
module UTS1_11 (
  input  x,
  input  y,
  input  z
);

  wire and_1_out, and_2_out, and_3_out, and_4_out, not_1_out, not_2_out, not_3_out, or_1_out;

  not not_1 (not_1_out, x);
  not not_2 (not_2_out, z);
  not not_3 (not_3_out, x);
  and and_1 (and_1_out, not_1_out, y, z);
  and and_2 (and_2_out, x, y, not_2_out);
  and and_3 (and_3_out, not_3_out, y, z);
  and and_4 (and_4_out, x, y);
  or or_1 (or_1_out, and_1_out, and_2_out, and_3_out, and_4_out);
  LED A (.in(or_1_out));

  // Notes on the sheet:
  //   FATIMAH CAHYANI IRAWAN
  //   NO 11. x'y'z' + xyz' + x'yz + xy
endmodule
