// Digital circuit UTS1_14.dig as structural Verilog
module UTS1_14 (
  input  x,
  input  y,
  input  z
);

  wire and_1_out, and_2_out, and_3_out, and_4_out, not_1_out, not_2_out, not_3_out, not_4_out, or_1_out;

  not not_1 (not_1_out, z);
  not not_2 (not_2_out, x);
  not not_3 (not_3_out, x);
  not not_4 (not_4_out, y);
  and and_1 (and_1_out, x, not_1_out);
  and and_2 (and_2_out, not_2_out, z);
  and and_3 (and_3_out, not_3_out, y);
  and and_4 (and_4_out, x, not_4_out);
  or or_1 (or_1_out, and_1_out, and_2_out, and_3_out, and_4_out);
  LED A (.in(or_1_out));

  // Notes on the sheet:
  //   FATIMAH CAHYANI IRAWAN
  //   NO 14. xz' + x'z + x'y + xy'
endmodule
