// Digital circuit UTS1_6.dig as structural Verilog
module UTS1_6 (
  input  A,
  input  B,
  input  C,
  input  D
);

  wire and_1_out, and_2_out, and_3_out, and_4_out, not_1_out, not_2_out, not_3_out, not_4_out, not_5_out,
       or_1_out;

  not not_1 (not_1_out, A);
  not not_2 (not_2_out, A);
  not not_3 (not_3_out, A);
  not not_4 (not_4_out, B);
  not not_5 (not_5_out, C);
  and and_1 (and_1_out, not_1_out, not_4_out, C);
  and and_2 (and_2_out, not_2_out, not_5_out, D);
  and and_3 (and_3_out, not_3_out, B, B);
  and and_4 (and_4_out, A, B, D);
  or or_1 (or_1_out, and_1_out, and_2_out, and_3_out, and_4_out);
  LED X (.in(or_1_out));

  // Notes on the sheet:
  //   NO 6. A'B'C' + A'C'D' + A'BC + ABD
  //   FATIMAH CAHYANI IRAWAN
endmodule
