// Digital circuit UTS1_7.dig as structural Verilog
module UTS1_7 (
  input  W,
  input  X,
  input  Y,
  input  Z
);

  wire and_1_out, and_2_out, and_3_out, and_4_out, not_1_out, not_2_out, not_3_out, not_4_out, or_1_out;

  not not_1 (not_1_out, X);
  not not_2 (not_2_out, Y);
  not not_3 (not_3_out, W);
  not not_4 (not_4_out, W);
  and and_1 (and_1_out, not_3_out, X);
  and and_2 (and_2_out, W, X, X);
  and and_3 (and_3_out, not_4_out, not_1_out, Z);
  and and_4 (and_4_out, X, not_2_out);
  or or_1 (or_1_out, and_3_out, and_4_out, and_1_out, and_2_out);
  LED A (.in(or_1_out));

  // Notes on the sheet:
  //   FATIMAH CAHYANI IRAWAN
  //   NO 7.  w'x'z' + xy' + w'x +wxy
endmodule
